// Logisim project CPU-RX0208.circ as structural Verilog: 23 circuits, main circuit main
module main (
  input  [7:0] in_1,
  input  in_2,
  input  in_3,
  output out_4,
  output out_5,
  output out_6,
  output out_7,
  output out_8,
  output out_9,
  output out_10,
  output out_11
);

  wire clock_1_out, cpu_1_readram, cpu_1_writeram;
  wire [7:0] cpu_1_busout, ram_1_data;
  wire [15:0] cpu_1_addresstoram;

  Clock clock_1 (.out(clock_1_out));
  CPU cpu_1 (
    .Ce(in_3), .BusOut(cpu_1_busout), .BusIN(in_1), .Rst(in_2), .DataFromRam(ram_1_data),
    .ReadRam(cpu_1_readram), .WriteRam(cpu_1_writeram), .AddressToRam(cpu_1_addresstoram), .Clk(clock_1_out));
  TTY tty_1 (.data(cpu_1_busout[6:0]), .clk(cpu_1_writeram));  // open: we, clr
  GPIO gpio_1 (
    .DataFromRAMC(cpu_1_busout), .str(cpu_1_writeram), .AddressFromRAMC(cpu_1_addresstoram),
    .SetAddress({16{1'b0}}), .clk(cpu_1_writeram), ._0(out_11), ._1(out_10), ._2(out_9), ._3(out_8),
    ._4(out_7), ._5(out_6), ._6(out_5), ._7(out_4));
  RAM #(.addrWidth(16), .bus("separate")) ram_1 (
    .addr(cpu_1_addresstoram), .din(cpu_1_busout), .data(ram_1_data), .str(cpu_1_writeram), .sel(1'b1),
    .clk(cpu_1_writeram), .ld(cpu_1_readram));  // open: clr

  // Notes on the sheet:
  //   RAM
endmodule

module Program_Counter (
  input  [7:0] FromRom,
  input  JumpFlag,
  input  [15:0] JumpTo,
  input  Clock,
  input  Clear,
  input  Run,
  input  [1:0] FromOPROM,
  input  JmpClk,
  output [15:0] RomAddress,
  output RunFlag,
  output [7:0] OP_Code,
  output End,
  output [23:0] Command,
  output CommandFlag,
  output [7:0] Data,
  output [7:0] Reg
);

  wire and_1_out, and_2_out, and_3_out, buffer_1_out, buffer_2_out, buffer_3_out, buffer_4_out, buffer_5_out,
       buffer_6_out, buffer_7_out, buffer_8_out, buffer_9_out, click_1_out_2, n2buffer_1_out_2, not_1_out,
       not_2_out, not_3_out, or_1_out, or_2_out, or_3_out, or_4_out;
  wire [1:0] counter_2_q;

  CLICK click_1 (.in_1(Clock), .out_2(click_1_out_2));
  Counter #(.width(16), .max('hffff)) counter_1 (
    .load(JumpFlag), .D(JumpTo), .count(and_1_out), .Q(RomAddress), .carry(End), .clk(or_1_out), .clr(Clear));
  buf buffer_1 (buffer_1_out, Run);
  and and_1 (and_1_out, buffer_1_out, not_1_out);
  not not_1 (not_1_out, JumpFlag);
  or or_1 (or_1_out, JmpClk, click_1_out_2);
  or or_2 (or_2_out, Clear, JumpFlag);
  or or_3 (or_3_out, or_2_out, and_2_out);
  buf buffer_2 (buffer_2_out, Clock);
  Counter #(.width(2), .max('h2)) counter_2 (
    .count(Run), .Q(counter_2_q), .clk(buffer_2_out), .clr(or_3_out));  // open: load, D, carry
  buf buffer_3 (buffer_3_out, buffer_4_out);
  buf buffer_4 (buffer_4_out, counter_2_q[1]);
  and and_2 (and_2_out, buffer_3_out, not_2_out);
  not not_2 (not_2_out, and_3_out);
  or or_4 (or_4_out, counter_2_q[0], counter_2_q[1]);
  buf buffer_5 (buffer_5_out, buffer_7_out);
  buf buffer_6 (buffer_6_out, buffer_2_out);
  buf buffer_7 (buffer_7_out, buffer_6_out);
  and and_3 (and_3_out, counter_2_q[1], FromOPROM[0]);
  Register register_1 (.D(FromRom), .en(not_3_out), .Q(OP_Code), .clk(buffer_5_out), .clr(or_2_out));
  not not_3 (not_3_out, or_4_out);
  Register register_2 (.D(FromRom), .en(counter_2_q[0]), .Q(Reg), .clk(buffer_5_out), .clr(or_2_out));
  Register register_3 (.D(FromRom), .en(and_3_out), .Q(Data), .clk(buffer_5_out), .clr(or_3_out));
  Register #(.width(24)) register_4 (
    .D({OP_Code, Reg, Data}), .en(Run), .Q(Command), .clk(buffer_8_out), .clr(or_2_out));
  buf buffer_8 (buffer_8_out, buffer_9_out);
  buf buffer_9 (buffer_9_out, not_3_out);
  _2Buffer u_2buffer_1 (.in_1(buffer_8_out), .out_2(n2buffer_1_out_2));
  _2Buffer u_2buffer_2 (.in_1(n2buffer_1_out_2), .out_2(CommandFlag));

  assign RunFlag = Run;
endmodule

module CPU (
  input  [7:0] BusIN,
  input  [7:0] DataFromRam,
  input  Clk,
  input  Rst,
  input  Ce,
  output [7:0] BusOut,
  output ReadRam,
  output [15:0] AddressToRam,
  output WriteRam
);

  wire alu_1_ch, alu_1_settflag, and_1_out, and_2_out, and_3_out, and_4_out, and_5_out, comparer_1_bt,
       comparer_1_eq, comparer_1_st, n2buffer_1_out_2, n8buffer_1_out_2, n8buffer_2_out_2, n8buffer_3_out_2,
       n8buffer_5_out_2, n8buffer_6_out_2, not_1_out, or_2_out, program_counter_1_commandflag, undriven;
  wire [1:0] rom_3_data;
  wire [7:0] A_q, alu_1_result, B_q, C_q, chooser_8bit_5_out_3, chooser_8bit_6_out_3, chooser_8bit_7_out_3,
       chooser_8bit_8_out_3, chooser_8bit_9_out_3, chooser_8bit_10_out_3, program_counter_1_data,
       program_counter_1_op_code, program_counter_1_reg, ram_1_data, rom_1_data;
  wire [15:0] chooser_8bit_1_out_3, chooser_8bit_3_out_3, program_counter_1_romaddress;
  wire [31:0] rom_2_data;

  assign AddressToRam = chooser_8bit_1_out_3 | chooser_8bit_3_out_3;  // OR_Gate or_1, 16 bits wide
  Chooser_8Bit chooser_8bit_1 (.in_1(rom_2_data[21]), .in_2(B_q), .out_3(chooser_8bit_1_out_3[7:0]));
  Chooser_8Bit chooser_8bit_2 (.in_1(rom_2_data[21]), .in_2(A_q), .out_3(chooser_8bit_1_out_3[15:8]));
  ROM #(.addrWidth(16)) rom_1 (.addr(program_counter_1_romaddress), .data(rom_1_data));  // open: sel
  Chooser_8Bit chooser_8bit_3 (.in_1(or_2_out), .in_2(program_counter_1_data), .out_3(chooser_8bit_3_out_3[7:0]));
  Chooser_8Bit chooser_8bit_4 (.in_1(or_2_out), .in_2(program_counter_1_reg), .out_3(chooser_8bit_3_out_3[15:8]));
  or or_2 (or_2_out, rom_2_data[22], and_1_out, and_2_out, and_3_out);
  Register A (.D(BusOut), .en(1'b1), .Q(A_q), .clk(n8buffer_6_out_2));  // open: clr
  Register B (.D(BusOut), .en(1'b1), .Q(B_q), .clk(n8buffer_5_out_2));  // open: clr
  and and_1 (and_1_out, comparer_1_st, rom_2_data[25]);
  and and_2 (and_2_out, comparer_1_eq, rom_2_data[26]);
  and and_3 (and_3_out, comparer_1_bt, rom_2_data[27]);
  _2Buffer u_2buffer_1 (.in_1(and_5_out), .out_2(n2buffer_1_out_2));
  Comparer comparer_1 (
    .FromA(A_q), .FromB(B_q), .BT(comparer_1_bt), .EQ(comparer_1_eq), .ST(comparer_1_st),
    .CLF(rom_2_data[24]), .CMP(rom_2_data[23]));
  RAM #(.bus("separate")) ram_1 (
    .addr(program_counter_1_reg), .din(BusOut), .data(ram_1_data), .str(n8buffer_3_out_2),
    .clk(n8buffer_3_out_2), .ld(rom_2_data[16]));  // open: sel, clr
  Program_Counter program_counter_1 (
    .FromRom(rom_1_data), .JumpFlag(and_5_out), .JumpTo(AddressToRam), .Clock(Clk), .Clear(Rst), .Run(Ce),
    .FromOPROM(rom_3_data), .RomAddress(program_counter_1_romaddress), .OP_Code(program_counter_1_op_code),
    .CommandFlag(program_counter_1_commandflag), .JmpClk(n2buffer_1_out_2), .Data(program_counter_1_data),
    .Reg(program_counter_1_reg));  // open: RunFlag, End, Command
  ALU alu_1 (
    .V1(A_q), .V2(B_q), .Result(alu_1_result), .SUM(rom_2_data[0]), .SUB(rom_2_data[1]), .OR(rom_2_data[2]),
    .AND(rom_2_data[3]), .XOR(rom_2_data[4]), .NOT(rom_2_data[5]), .LM(rom_2_data[6]), .RM(rom_2_data[7]),
    .LMT(rom_2_data[8]), .RMT(rom_2_data[9]), .TempFlag(undriven), .BC(rom_2_data[10]),
    .SetTflag(alu_1_settflag), .SBT(rom_2_data[11]), .CH(alu_1_ch));
  Chooser_8Bit chooser_8bit_5 (.in_1(rom_2_data[19]), .in_2(C_q), .out_3(chooser_8bit_5_out_3));
  Register C (.D(BusOut), .en(1'b1), .Q(C_q), .clk(n8buffer_2_out_2));  // open: clr
  Chooser_8Bit chooser_8bit_6 (.in_1(rom_2_data[16]), .in_2(ram_1_data), .out_3(chooser_8bit_6_out_3));
  Chooser_8Bit chooser_8bit_7 (.in_1(ReadRam), .in_2(DataFromRam), .out_3(chooser_8bit_7_out_3));
  Chooser_8Bit chooser_8bit_8 (.in_1(rom_2_data[18]), .in_2(program_counter_1_data), .out_3(chooser_8bit_8_out_3));
  Chooser_8Bit chooser_8bit_9 (.in_1(alu_1_ch), .in_2(alu_1_result), .out_3(chooser_8bit_9_out_3));
  Hex_Digit_Display hex_digit_display_1 (.value(BusOut[3:0]));  // open: dp
  Hex_Digit_Display hex_digit_display_2 (.value(BusOut[7:4]));  // open: dp
  assign BusOut = BusIN | chooser_8bit_7_out_3 | chooser_8bit_6_out_3 | chooser_8bit_9_out_3 | chooser_8bit_5_out_3 | chooser_8bit_8_out_3;  // OR_Gate or_3, 8 bits wide
  and and_4 (and_4_out, program_counter_1_commandflag, not_1_out);
  not not_1 (not_1_out, Clk);
  Chooser_8Bit chooser_8bit_10 (.in_1(and_4_out), .in_2(program_counter_1_op_code), .out_3(chooser_8bit_10_out_3));
  and and_5 (and_5_out, n8buffer_1_out_2, or_2_out);
  _8Buffer u_8buffer_1 (.in_1(rom_2_data[31]), .out_2(n8buffer_1_out_2));
  _8Buffer u_8buffer_2 (.in_1(rom_2_data[20]), .out_2(n8buffer_2_out_2));
  _8Buffer u_8buffer_3 (.in_1(rom_2_data[17]), .out_2(n8buffer_3_out_2));
  _8Buffer u_8buffer_4 (.in_1(rom_2_data[15]), .out_2(WriteRam));
  _8Buffer u_8buffer_5 (.in_1(rom_2_data[13]), .out_2(n8buffer_5_out_2));
  _8Buffer u_8buffer_6 (.in_1(rom_2_data[12]), .out_2(n8buffer_6_out_2));
  ROM #(.dataWidth(32)) rom_2 (
    .addr(chooser_8bit_10_out_3), .data({rom_2_data[31:15], ReadRam, rom_2_data[13:0]}));  // open: sel
  ROM #(.dataWidth(2)) rom_3 (.addr(program_counter_1_op_code), .data(rom_3_data));  // open: sel

  // Notes on the sheet:
  //   ROM
  //   contents of rom_1 (hex, n*v repeats v):
  //   d 0 0 d 1 10 b 0 c 1 18 0 1a 0 12 1b 0 1a f 0 1 1 0 17 0 6 11 0 17
  //   Register
  //   Data BUS
  //   RX0208
  //   contents of rom_2 (hex, n*v repeats v):
  //   0 20001 20002 20004 20008 20010 20020 20040 20080 20100 20200 11000 12000 60000 41000 42000 c0000
  //   110000 120000 288000 84000 48000 80200000 80400000 800000 88000000 82000000 84000000
  //   OPcode
  //   MicroCode
  //   contents of rom_3 (hex, n*v repeats v):
  //   13*0 4*1 4*0 1 0 1 0 1 1 1
endmodule

module Register_Controller (
  input  [7:0] SaveToData,
  input  [3:0] Reg2,
  input  [7:0] ReadFromREG,
  input  [3:0] Reg1,
  input  LoadREG,
  input  SaveReg1,
  output [7:0] SaveToREG_prime_sData,
  output [3:0] AddressToREG,
  output str,
  output clk,
  output ldr,
  output [7:0] Reg2_2,
  output [7:0] Reg1_2
);

  wire and_4_out, buffer_1_out, buffer_3_out, click_1_out_2, click_2_out_2, n2buffer_1_out_2,
       n2buffer_2_out_2, n2buffer_3_out_2, n8buffer_1_out_2, not_1_out, or_1_out;
  wire [3:0] and_1_out, and_2_out, and_3_out, bit_extender_1_out, bit_extender_2_out, bit_extender_3_out;

  CLICK click_1 (.in_1(n8buffer_1_out_2), .out_2(click_1_out_2));
  _8Buffer u_8buffer_1 (.in_1(LoadREG), .out_2(n8buffer_1_out_2));
  CLICK click_2 (.in_1(LoadREG), .out_2(click_2_out_2));
  assign bit_extender_1_out = {{3{click_1_out_2}}, click_1_out_2};  // Bit_Extender bit_extender_1
  assign and_1_out = bit_extender_1_out & Reg2;  // AND_Gate and_1, 4 bits wide
  or or_1 (or_1_out, click_1_out_2, click_2_out_2);
  assign bit_extender_2_out = {{3{click_2_out_2}}, click_2_out_2};  // Bit_Extender bit_extender_2
  assign and_2_out = bit_extender_2_out & Reg1;  // AND_Gate and_2, 4 bits wide
  assign bit_extender_3_out = {{3{SaveReg1}}, SaveReg1};  // Bit_Extender bit_extender_3
  assign and_3_out = bit_extender_3_out & Reg1;  // AND_Gate and_3, 4 bits wide
  assign AddressToREG = and_1_out | and_3_out | and_2_out;  // OR_Gate or_2, 4 bits wide
  buf buffer_1 (buffer_1_out, or_1_out);
  buf buffer_2 (ldr, buffer_1_out);
  CLICK click_3 (.in_1(buffer_3_out), .out_2(clk));
  buf buffer_3 (buffer_3_out, SaveReg1);
  _2Buffer u_2buffer_1 (.in_1(n2buffer_3_out_2), .out_2(n2buffer_1_out_2));
  _2Buffer u_2buffer_2 (.in_1(ldr), .out_2(n2buffer_2_out_2));
  _2Buffer u_2buffer_3 (.in_1(n2buffer_2_out_2), .out_2(n2buffer_3_out_2));
  Register register_1 (.D(ReadFromREG), .en(n8buffer_1_out_2), .Q(Reg2_2), .clk(n2buffer_1_out_2));  // open: clr
  not not_1 (not_1_out, n8buffer_1_out_2);
  Register register_2 (.D(ReadFromREG), .en(and_4_out), .Q(Reg1_2), .clk(n2buffer_1_out_2));  // open: clr
  and and_4 (and_4_out, not_1_out, LoadREG);

  assign SaveToREG_prime_sData = SaveToData;
  assign str = SaveReg1;
endmodule

module CLICK (
  input  in_1,
  output out_2
);

  wire n2buffer_1_out_2, xor_1_out;

  _2Buffer u_2buffer_1 (.in_1(in_1), .out_2(n2buffer_1_out_2));
  xor xor_1 (xor_1_out, n2buffer_1_out_2, in_1);
  and and_1 (out_2, xor_1_out, in_1);
endmodule

module _2Buffer (
  input  in_1,
  output out_2
);

  wire buffer_2_out;

  buf buffer_1 (out_2, buffer_2_out);
  buf buffer_2 (buffer_2_out, in_1);
endmodule

module _8Buffer (
  input  in_1,
  output out_2
);

  wire n2buffer_1_out_2, n2buffer_2_out_2, n2buffer_3_out_2;

  _2Buffer u_2buffer_1 (.in_1(in_1), .out_2(n2buffer_1_out_2));
  _2Buffer u_2buffer_2 (.in_1(n2buffer_3_out_2), .out_2(n2buffer_2_out_2));
  _2Buffer u_2buffer_3 (.in_1(n2buffer_1_out_2), .out_2(n2buffer_3_out_2));
  _2Buffer u_2buffer_4 (.in_1(n2buffer_2_out_2), .out_2(out_2));
endmodule

module _16TickClick (
  input  in_1,
  output out_2
);

  wire n8buffer_1_out_2, n8buffer_2_out_2, xor_1_out;

  _8Buffer u_8buffer_1 (.in_1(n8buffer_2_out_2), .out_2(n8buffer_1_out_2));
  _8Buffer u_8buffer_2 (.in_1(in_1), .out_2(n8buffer_2_out_2));
  xor xor_1 (xor_1_out, n8buffer_1_out_2, in_1);
  and and_1 (out_2, xor_1_out, in_1);
endmodule

module ALU (
  input  SUM,
  input  SUB,
  input  OR,
  input  AND,
  input  XOR,
  input  NOT,
  input  LM,
  input  RM,
  input  LMT,
  input  RMT,
  input  BC,
  input  SBT,
  input  TempFlag,
  input  [7:0] V1,
  input  [7:0] V2,
  output CH,
  output [7:0] Result,
  output SetTflag
);

  wire and_3_out, bit_to_tempflag_1_result;
  wire [7:0] adder_1_out, and_1_out, and_2_out, and_4_out, and_5_out, and_6_out, and_7_out, and_8_out,
       and_9_out, and_10_out, and_11_out, and_12_out, and_13_out, bit_controller_1_result,
       bit_extender_1_out, bit_extender_2_out, bit_extender_3_out, bit_extender_4_out, bit_extender_5_out,
       bit_extender_6_out, bit_extender_7_out, bit_extender_8_out, bit_extender_9_out, bit_extender_10_out,
       bit_extender_11_out, not_1_out, or_1_out, subtractor_1_out, xor_1_out;

  Adder adder_1 (.a(V1), .b(V2), .out(adder_1_out), .cin(1'b0));  // open: cout
  Subtractor subtractor_1 (.a(V1), .b(V2), .out(subtractor_1_out), .bin(1'b0));  // open: bout
  assign or_1_out = V1 | V2;  // OR_Gate or_1, 8 bits wide
  assign and_1_out = V1 & V2;  // AND_Gate and_1, 8 bits wide
  assign xor_1_out = V1 ^ V2;  // XOR_Gate xor_1, 8 bits wide
  assign not_1_out = ~V1;  // NOT_Gate not_1, 8 bits wide
  Bit_Controller bit_controller_1 (.TempFlag(TempFlag), .Volum0(V1), .Volum1(V2), .Result(bit_controller_1_result));
  Bit_To_TempFlag bit_to_tempflag_1 (.Volum0(V1), .Volum1(V2), .Result(bit_to_tempflag_1_result));
  assign bit_extender_1_out = {{7{BC}}, BC};  // Bit_Extender bit_extender_1
  assign and_2_out = bit_extender_1_out & bit_controller_1_result;  // AND_Gate and_2, 8 bits wide
  CLICK click_1 (.in_1(and_3_out), .out_2(SetTflag));
  and and_3 (and_3_out, bit_to_tempflag_1_result, SBT);
  or or_2 (CH, SUM, SUB, OR, AND, XOR, NOT, LM, RM, LMT, RMT, BC, SBT);
  assign bit_extender_2_out = {{7{SUM}}, SUM};  // Bit_Extender bit_extender_2
  assign and_4_out = bit_extender_2_out & adder_1_out;  // AND_Gate and_4, 8 bits wide
  assign bit_extender_3_out = {{7{SUB}}, SUB};  // Bit_Extender bit_extender_3
  assign and_5_out = bit_extender_3_out & subtractor_1_out;  // AND_Gate and_5, 8 bits wide
  assign bit_extender_4_out = {{7{OR}}, OR};  // Bit_Extender bit_extender_4
  assign and_6_out = bit_extender_4_out & or_1_out;  // AND_Gate and_6, 8 bits wide
  assign bit_extender_5_out = {{7{AND}}, AND};  // Bit_Extender bit_extender_5
  assign and_7_out = bit_extender_5_out & and_1_out;  // AND_Gate and_7, 8 bits wide
  assign bit_extender_6_out = {{7{XOR}}, XOR};  // Bit_Extender bit_extender_6
  assign and_8_out = bit_extender_6_out & xor_1_out;  // AND_Gate and_8, 8 bits wide
  assign bit_extender_7_out = {{7{NOT}}, NOT};  // Bit_Extender bit_extender_7
  assign and_9_out = bit_extender_7_out & not_1_out;  // AND_Gate and_9, 8 bits wide
  assign bit_extender_8_out = {{7{LM}}, LM};  // Bit_Extender bit_extender_8
  assign and_10_out = bit_extender_8_out & {V1[6:0], 1'b0};  // AND_Gate and_10, 8 bits wide
  assign bit_extender_9_out = {{7{RM}}, RM};  // Bit_Extender bit_extender_9
  assign and_11_out = bit_extender_9_out & {1'b0, V1[7:1]};  // AND_Gate and_11, 8 bits wide
  assign bit_extender_10_out = {{7{LMT}}, LMT};  // Bit_Extender bit_extender_10
  assign and_12_out = bit_extender_10_out & {V1[6:0], V1[7]};  // AND_Gate and_12, 8 bits wide
  assign bit_extender_11_out = {{7{RMT}}, RMT};  // Bit_Extender bit_extender_11
  assign and_13_out = bit_extender_11_out & {V1[0], V1[7:1]};  // AND_Gate and_13, 8 bits wide
  assign Result = and_4_out | and_5_out | and_2_out | and_6_out | and_7_out | and_8_out | and_9_out | and_10_out | and_11_out | and_12_out | and_13_out;  // OR_Gate or_3, 8 bits wide

  // Notes on the sheet:
  //   LM
  //   RM
  //   LMT
  //   RMT
endmodule

module ALU_Controller (
  input  TempFlag,
  input  [7:0] FromReg1,
  input  [7:0] FromReg2,
  input  [23:0] Command,
  output TempFlag_2,
  output [7:0] ToV1,
  output [7:0] ToV2,
  output LoadReg,
  output Cache_prime_sClk,
  output ADD,
  output SUB,
  output CacheFlag,
  output OR,
  output AND,
  output XOR,
  output NOT,
  output LM,
  output RM,
  output LMT,
  output [3:0] Reg1,
  output RMT,
  output BC,
  output STB,
  output [3:0] Reg2
);

  wire comparator_1_eq, comparator_2_eq, comparator_11_eq, comparator_12_eq, n2buffer_1_out_2,
       n2buffer_2_out_2, n2buffer_3_out_2, n2buffer_4_out_2, n2buffer_5_out_2, n2buffer_6_out_2,
       n2buffer_7_out_2, n2buffer_8_out_2, n2buffer_9_out_2, n2buffer_10_out_2, n2buffer_11_out_2,
       n2buffer_12_out_2, n2buffer_13_out_2, n2buffer_14_out_2, n2buffer_15_out_2, n2buffer_16_out_2,
       n2buffer_17_out_2, n2buffer_18_out_2, n2buffer_19_out_2, n2buffer_20_out_2, n2buffer_21_out_2,
       n2buffer_22_out_2, n2buffer_23_out_2, n2buffer_24_out_2, n8buffer_1_out_2, n8buffer_2_out_2,
       n8buffer_3_out_2, n8buffer_4_out_2, n8buffer_5_out_2, n8buffer_6_out_2, n16tickclick_1_out_2,
       n16tickclick_2_out_2, n16tickclick_3_out_2, n16tickclick_4_out_2, n16tickclick_5_out_2,
       n16tickclick_6_out_2, n16tickclick_7_out_2, n16tickclick_8_out_2, n16tickclick_9_out_2,
       n16tickclick_10_out_2, n16tickclick_11_out_2, n16tickclick_12_out_2, or_1_out, or_4_out, or_6_out;
  wire [3:0] bit_extender_1_out, bit_extender_2_out;
  wire [7:0] and_3_out, and_4_out, bit_extender_3_out, bit_extender_4_out;

  assign bit_extender_1_out = {{3{or_1_out}}, or_1_out};  // Bit_Extender bit_extender_1
  assign bit_extender_2_out = {{3{or_4_out}}, or_4_out};  // Bit_Extender bit_extender_2
  assign Reg1 = bit_extender_1_out & Command[15:12];  // AND_Gate and_1, 4 bits wide
  assign Reg2 = bit_extender_2_out & Command[11:8];  // AND_Gate and_2, 4 bits wide
  Comparator comparator_1 (.a(Command[23:16]), .b(8'h1), .eq(comparator_1_eq));  // open: gt, lt
  Comparator comparator_2 (.a(Command[23:16]), .b(8'h2), .eq(comparator_2_eq));  // open: gt, lt
  Comparator comparator_3 (.a(Command[23:16]), .b(8'h3), .eq(OR));  // open: gt, lt
  Comparator comparator_4 (.a(Command[23:16]), .b(8'h4), .eq(AND));  // open: gt, lt
  Comparator comparator_5 (.a(Command[23:16]), .b(8'h5), .eq(XOR));  // open: gt, lt
  Comparator comparator_6 (.a(Command[23:16]), .b(8'h6), .eq(NOT));  // open: gt, lt
  Comparator comparator_7 (.a(Command[23:16]), .b(8'h7), .eq(LM));  // open: gt, lt
  Comparator comparator_8 (.a(Command[23:16]), .b(8'h8), .eq(RM));  // open: gt, lt
  Comparator comparator_9 (.a(Command[23:16]), .b(8'h9), .eq(LMT));  // open: gt, lt
  Comparator comparator_10 (.a(Command[23:16]), .b(8'ha), .eq(RMT));  // open: gt, lt
  or or_1 (or_1_out, STB, NOT, LM, OR, comparator_11_eq, comparator_1_eq, comparator_2_eq, AND, XOR, comparator_12_eq, BC, RM, LMT, RMT);
  assign bit_extender_3_out = {{7{or_4_out}}, or_4_out};  // Bit_Extender bit_extender_3
  assign and_3_out = bit_extender_3_out & FromReg2;  // AND_Gate and_3, 8 bits wide
  or or_2 (ADD, comparator_1_eq, comparator_11_eq);
  or or_3 (SUB, comparator_2_eq, comparator_12_eq);
  or or_4 (or_4_out, comparator_1_eq, comparator_2_eq, OR, XOR, AND, AND);
  Comparator comparator_11 (.a(Command[23:16]), .b(8'hb), .eq(comparator_11_eq));  // open: gt, lt
  Comparator comparator_12 (.a(Command[23:16]), .b(8'hc), .eq(comparator_12_eq));  // open: gt, lt
  assign ToV2 = and_3_out | and_4_out;  // OR_Gate or_5, 8 bits wide
  or or_6 (or_6_out, BC, comparator_11_eq, comparator_12_eq, STB);
  assign bit_extender_4_out = {{7{or_6_out}}, or_6_out};  // Bit_Extender bit_extender_4
  assign and_4_out = bit_extender_4_out & Command[7:0];  // AND_Gate and_4, 8 bits wide
  _2Buffer u_2buffer_1 (.in_1(BC), .out_2(n2buffer_1_out_2));
  _2Buffer u_2buffer_2 (.in_1(ADD), .out_2(n2buffer_2_out_2));
  _2Buffer u_2buffer_3 (.in_1(SUB), .out_2(n2buffer_3_out_2));
  _2Buffer u_2buffer_4 (.in_1(OR), .out_2(n2buffer_4_out_2));
  _2Buffer u_2buffer_5 (.in_1(AND), .out_2(n2buffer_5_out_2));
  _2Buffer u_2buffer_6 (.in_1(XOR), .out_2(n2buffer_6_out_2));
  or or_7 (CacheFlag, BC, ADD, SUB, OR, AND, XOR, NOT, LM, RM, LMT, RMT, STB);
  _2Buffer u_2buffer_7 (.in_1(NOT), .out_2(n2buffer_7_out_2));
  _2Buffer u_2buffer_8 (.in_1(LM), .out_2(n2buffer_8_out_2));
  _2Buffer u_2buffer_9 (.in_1(RM), .out_2(n2buffer_9_out_2));
  _2Buffer u_2buffer_10 (.in_1(LMT), .out_2(n2buffer_10_out_2));
  _2Buffer u_2buffer_11 (.in_1(RMT), .out_2(n2buffer_11_out_2));
  _2Buffer u_2buffer_12 (.in_1(STB), .out_2(n2buffer_12_out_2));
  _2Buffer u_2buffer_13 (.in_1(n2buffer_1_out_2), .out_2(n2buffer_13_out_2));
  _16TickClick u_16tickclick_1 (.in_1(n2buffer_13_out_2), .out_2(n16tickclick_1_out_2));
  _16TickClick u_16tickclick_2 (.in_1(n2buffer_14_out_2), .out_2(n16tickclick_2_out_2));
  _2Buffer u_2buffer_14 (.in_1(n2buffer_2_out_2), .out_2(n2buffer_14_out_2));
  _2Buffer u_2buffer_15 (.in_1(n2buffer_3_out_2), .out_2(n2buffer_15_out_2));
  _16TickClick u_16tickclick_3 (.in_1(n2buffer_15_out_2), .out_2(n16tickclick_3_out_2));
  _16TickClick u_16tickclick_4 (.in_1(n2buffer_16_out_2), .out_2(n16tickclick_4_out_2));
  _2Buffer u_2buffer_16 (.in_1(n2buffer_4_out_2), .out_2(n2buffer_16_out_2));
  _2Buffer u_2buffer_17 (.in_1(n2buffer_5_out_2), .out_2(n2buffer_17_out_2));
  _16TickClick u_16tickclick_5 (.in_1(n2buffer_17_out_2), .out_2(n16tickclick_5_out_2));
  _2Buffer u_2buffer_18 (.in_1(n2buffer_6_out_2), .out_2(n2buffer_18_out_2));
  _16TickClick u_16tickclick_6 (.in_1(n2buffer_18_out_2), .out_2(n16tickclick_6_out_2));
  _16TickClick u_16tickclick_7 (.in_1(n2buffer_19_out_2), .out_2(n16tickclick_7_out_2));
  _2Buffer u_2buffer_19 (.in_1(n2buffer_7_out_2), .out_2(n2buffer_19_out_2));
  _16TickClick u_16tickclick_8 (.in_1(n2buffer_20_out_2), .out_2(n16tickclick_8_out_2));
  _2Buffer u_2buffer_20 (.in_1(n2buffer_8_out_2), .out_2(n2buffer_20_out_2));
  _2Buffer u_2buffer_21 (.in_1(n2buffer_9_out_2), .out_2(n2buffer_21_out_2));
  _16TickClick u_16tickclick_9 (.in_1(n2buffer_21_out_2), .out_2(n16tickclick_9_out_2));
  _16TickClick u_16tickclick_10 (.in_1(n2buffer_22_out_2), .out_2(n16tickclick_10_out_2));
  _2Buffer u_2buffer_22 (.in_1(n2buffer_10_out_2), .out_2(n2buffer_22_out_2));
  _2Buffer u_2buffer_23 (.in_1(n2buffer_11_out_2), .out_2(n2buffer_23_out_2));
  _16TickClick u_16tickclick_11 (.in_1(n2buffer_23_out_2), .out_2(n16tickclick_11_out_2));
  _16TickClick u_16tickclick_12 (.in_1(n2buffer_24_out_2), .out_2(n16tickclick_12_out_2));
  _2Buffer u_2buffer_24 (.in_1(n2buffer_12_out_2), .out_2(n2buffer_24_out_2));
  Comparator comparator_13 (.a(Command[23:16]), .b(8'he), .eq(STB));  // open: gt, lt
  Comparator comparator_14 (.a(Command[23:16]), .b(8'hf), .eq(BC));  // open: gt, lt
  or or_8 (LoadReg, n16tickclick_1_out_2, n16tickclick_2_out_2, n16tickclick_3_out_2, n16tickclick_4_out_2, n16tickclick_5_out_2, n16tickclick_6_out_2, n16tickclick_7_out_2, n16tickclick_8_out_2, n16tickclick_9_out_2, n16tickclick_10_out_2, n16tickclick_11_out_2, n16tickclick_12_out_2);
  _8Buffer u_8buffer_1 (.in_1(n8buffer_6_out_2), .out_2(n8buffer_1_out_2));
  _8Buffer u_8buffer_2 (.in_1(n8buffer_4_out_2), .out_2(n8buffer_2_out_2));
  _8Buffer u_8buffer_3 (.in_1(CacheFlag), .out_2(n8buffer_3_out_2));
  _8Buffer u_8buffer_4 (.in_1(n8buffer_3_out_2), .out_2(n8buffer_4_out_2));
  _8Buffer u_8buffer_5 (.in_1(n8buffer_1_out_2), .out_2(n8buffer_5_out_2));
  _8Buffer u_8buffer_6 (.in_1(n8buffer_2_out_2), .out_2(n8buffer_6_out_2));
  CLICK click_1 (.in_1(n8buffer_5_out_2), .out_2(Cache_prime_sClk));

  assign TempFlag_2 = TempFlag;
  assign ToV1 = FromReg1;

  // Notes on the sheet:
  //   ADD
  //   SUB
  //   OR
  //   AND
  //   XOR
  //   NOT
  //   LM
  //   RM
  //   LMT
  //   RMT
  //   ADDI
  //   SUBI
  //   SBT
  //   BC
endmodule

module Move_Manager (
  input  [7:0] Data_from_Reg2,
  input  [7:0] Data_from_Reg1,
  input  [7:0] DataFromRAMC,
  input  [7:0] DataFromCache,
  input  [23:0] Command,
  output [15:0] out_6,
  output [7:0] ToRegisterData,
  output SaveRegisterFlag,
  output [7:0] DataToCache,
  output SavaToCacheCLK,
  output SaveToCacheFLAG,
  output [7:0] SaveRamData,
  output [15:0] ToRamAddress,
  output SaveRamFlag,
  output ReadRamFlag,
  output ToClearCache,
  output ToClearRegister,
  output ToClearRam,
  output ToClearFlags,
  output ToReset,
  output Load_Reg_flag,
  output [3:0] Reg1,
  output [3:0] Reg2
);

  wire click_5_out_2, comparator_1_eq, comparator_2_eq, comparator_3_eq, comparator_4_eq, comparator_5_eq,
       comparator_6_eq, comparator_7_eq, comparator_8_eq, comparator_9_eq, comparator_11_eq,
       comparator_12_eq, n2buffer_1_out_2, n2buffer_2_out_2, n2buffer_3_out_2, n2buffer_4_out_2,
       n2buffer_5_out_2, n2buffer_6_out_2, n2buffer_7_out_2, n2buffer_8_out_2, n2buffer_9_out_2,
       n2buffer_10_out_2, n2buffer_11_out_2, n8buffer_1_out_2, n8buffer_2_out_2, n8buffer_3_out_2,
       n8buffer_4_out_2, n8buffer_5_out_2, n8buffer_6_out_2, n8buffer_7_out_2, n8buffer_8_out_2,
       n8buffer_9_out_2, n8buffer_10_out_2, n16tickclick_1_out_2, n16tickclick_2_out_2, n16tickclick_3_out_2,
       n16tickclick_4_out_2, n16tickclick_5_out_2, or_1_out, or_2_out, or_3_out, or_4_out, or_5_out,
       or_6_out, or_7_out, or_8_out, or_9_out;
  wire [3:0] bit_extender_2_out, bit_extender_3_out;
  wire [7:0] and_4_out, and_5_out, and_6_out, and_8_out, bit_extender_4_out, bit_extender_5_out,
       bit_extender_6_out, bit_extender_8_out;
  wire [15:0] and_1_out, and_7_out, bit_extender_1_out, bit_extender_7_out;

  assign bit_extender_1_out = {{15{or_1_out}}, or_1_out};  // Bit_Extender bit_extender_1
  or or_1 (or_1_out, comparator_11_eq, comparator_12_eq);
  assign and_1_out = bit_extender_1_out & {Data_from_Reg1, Data_from_Reg2};  // AND_Gate and_1, 16 bits wide
  Comparator comparator_1 (.a(Command[23:16]), .b(8'h11), .eq(comparator_1_eq));  // open: gt, lt
  Comparator comparator_2 (.a(Command[23:16]), .b(8'h12), .eq(comparator_2_eq));  // open: gt, lt
  Comparator comparator_3 (.a(Command[23:16]), .b(8'h13), .eq(comparator_3_eq));  // open: gt, lt
  Comparator comparator_4 (.a(Command[23:16]), .b(8'h14), .eq(comparator_4_eq));  // open: gt, lt
  Comparator comparator_5 (.a(Command[23:16]), .b(8'h15), .eq(comparator_5_eq));  // open: gt, lt
  Comparator comparator_6 (.a(Command[23:16]), .b(8'h16), .eq(comparator_6_eq));  // open: gt, lt
  Comparator comparator_7 (.a(Command[23:16]), .b(8'h17), .eq(comparator_7_eq));  // open: gt, lt
  Comparator comparator_8 (.a(Command[23:16]), .b(8'h18), .eq(comparator_8_eq));  // open: gt, lt
  Comparator comparator_9 (.a(Command[23:16]), .b(8'h19), .eq(comparator_9_eq));  // open: gt, lt
  Comparator comparator_10 (.a(Command[23:16]), .b(8'h1a), .eq(ToReset));  // open: gt, lt
  Comparator comparator_11 (.a(Command[23:16]), .b(8'h1b), .eq(comparator_11_eq));  // open: gt, lt
  Comparator comparator_12 (.a(Command[23:16]), .b(8'h1c), .eq(comparator_12_eq));  // open: gt, lt
  or or_2 (or_2_out, comparator_12_eq, comparator_3_eq, comparator_1_eq, comparator_11_eq);
  or or_3 (or_3_out, comparator_12_eq, comparator_11_eq);
  assign bit_extender_2_out = {{3{or_3_out}}, or_3_out};  // Bit_Extender bit_extender_2
  _8Buffer u_8buffer_1 (.in_1(comparator_4_eq), .out_2(n8buffer_1_out_2));
  _16TickClick u_16tickclick_1 (.in_1(n8buffer_3_out_2), .out_2(n16tickclick_1_out_2));
  _2Buffer u_2buffer_1 (.in_1(comparator_12_eq), .out_2(n2buffer_1_out_2));
  _2Buffer u_2buffer_2 (.in_1(comparator_11_eq), .out_2(n2buffer_2_out_2));
  assign bit_extender_3_out = {{3{or_2_out}}, or_2_out};  // Bit_Extender bit_extender_3
  assign Reg1 = bit_extender_3_out & Command[15:12];  // AND_Gate and_2, 4 bits wide
  assign Reg2 = bit_extender_2_out & Command[11:8];  // AND_Gate and_3, 4 bits wide
  assign bit_extender_4_out = {{7{comparator_1_eq}}, comparator_1_eq};  // Bit_Extender bit_extender_4
  assign and_4_out = bit_extender_4_out & Command[7:0];  // AND_Gate and_4, 8 bits wide
  _2Buffer u_2buffer_3 (.in_1(n2buffer_4_out_2), .out_2(n2buffer_3_out_2));
  _2Buffer u_2buffer_4 (.in_1(comparator_1_eq), .out_2(n2buffer_4_out_2));
  assign bit_extender_5_out = {{7{comparator_2_eq}}, comparator_2_eq};  // Bit_Extender bit_extender_5
  assign and_5_out = bit_extender_5_out & Command[15:8];  // AND_Gate and_5, 8 bits wide
  _2Buffer u_2buffer_5 (.in_1(comparator_2_eq), .out_2(n2buffer_5_out_2));
  _2Buffer u_2buffer_6 (.in_1(n2buffer_5_out_2), .out_2(n2buffer_6_out_2));
  assign bit_extender_6_out = {{7{comparator_3_eq}}, comparator_3_eq};  // Bit_Extender bit_extender_6
  assign and_6_out = bit_extender_6_out & DataFromCache;  // AND_Gate and_6, 8 bits wide
  _2Buffer u_2buffer_7 (.in_1(comparator_3_eq), .out_2(n2buffer_7_out_2));
  _2Buffer u_2buffer_8 (.in_1(n2buffer_7_out_2), .out_2(n2buffer_8_out_2));
  assign bit_extender_7_out = {{15{or_4_out}}, or_4_out};  // Bit_Extender bit_extender_7
  or or_4 (or_4_out, comparator_4_eq, comparator_5_eq);
  _2Buffer u_2buffer_9 (.in_1(n8buffer_1_out_2), .out_2(n2buffer_9_out_2));
  _16TickClick u_16tickclick_2 (.in_1(n2buffer_9_out_2), .out_2(n16tickclick_2_out_2));
  CLICK click_1 (.in_1(or_5_out), .out_2(ToClearCache));
  or or_5 (or_5_out, comparator_6_eq, ToReset);
  or or_6 (or_6_out, comparator_7_eq, ToReset);
  CLICK click_2 (.in_1(or_6_out), .out_2(ToClearRegister));
  CLICK click_3 (.in_1(or_7_out), .out_2(ToClearRam));
  or or_7 (or_7_out, comparator_8_eq, ToReset);
  CLICK click_4 (.in_1(or_8_out), .out_2(ToClearFlags));
  or or_8 (or_8_out, comparator_9_eq, ToReset);
  _8Buffer u_8buffer_2 (.in_1(n8buffer_5_out_2), .out_2(n8buffer_2_out_2));
  _8Buffer u_8buffer_3 (.in_1(n8buffer_4_out_2), .out_2(n8buffer_3_out_2));
  _8Buffer u_8buffer_4 (.in_1(n8buffer_7_out_2), .out_2(n8buffer_4_out_2));
  _8Buffer u_8buffer_5 (.in_1(n8buffer_6_out_2), .out_2(n8buffer_5_out_2));
  _8Buffer u_8buffer_6 (.in_1(n2buffer_10_out_2), .out_2(n8buffer_6_out_2));
  _8Buffer u_8buffer_7 (.in_1(n2buffer_11_out_2), .out_2(n8buffer_7_out_2));
  _2Buffer u_2buffer_10 (.in_1(n2buffer_1_out_2), .out_2(n2buffer_10_out_2));
  _2Buffer u_2buffer_11 (.in_1(n2buffer_2_out_2), .out_2(n2buffer_11_out_2));
  _16TickClick u_16tickclick_3 (.in_1(n2buffer_3_out_2), .out_2(n16tickclick_3_out_2));
  CLICK click_5 (.in_1(n2buffer_6_out_2), .out_2(click_5_out_2));
  _16TickClick u_16tickclick_4 (.in_1(n2buffer_8_out_2), .out_2(n16tickclick_4_out_2));
  assign and_7_out = bit_extender_7_out & Command[15:0];  // AND_Gate and_7, 16 bits wide
  assign bit_extender_8_out = {{7{or_9_out}}, or_9_out};  // Bit_Extender bit_extender_8
  assign and_8_out = bit_extender_8_out & DataFromRAMC;  // AND_Gate and_8, 8 bits wide
  or or_9 (or_9_out, n8buffer_2_out_2, comparator_5_eq);
  or or_10 (Load_Reg_flag, n2buffer_10_out_2, n2buffer_11_out_2);
  assign ToRegisterData = and_4_out | and_6_out;  // OR_Gate or_11, 8 bits wide
  or or_12 (SaveRegisterFlag, n16tickclick_3_out_2, n16tickclick_4_out_2);
  assign DataToCache = and_8_out | and_5_out;  // OR_Gate or_13, 8 bits wide
  or or_14 (SavaToCacheCLK, n16tickclick_5_out_2, click_5_out_2);
  or or_15 (SaveRamFlag, n16tickclick_2_out_2, n16tickclick_1_out_2);
  _16TickClick u_16tickclick_5 (.in_1(n8buffer_10_out_2), .out_2(n16tickclick_5_out_2));
  _8Buffer u_8buffer_8 (.in_1(or_9_out), .out_2(n8buffer_8_out_2));
  _8Buffer u_8buffer_9 (.in_1(n8buffer_8_out_2), .out_2(n8buffer_9_out_2));
  _8Buffer u_8buffer_10 (.in_1(n8buffer_9_out_2), .out_2(n8buffer_10_out_2));
  or or_16 (SaveToCacheFLAG, n2buffer_5_out_2, comparator_12_eq, comparator_5_eq);
  assign ToRamAddress = and_1_out | and_7_out;  // OR_Gate or_17, 16 bits wide
  CLICK click_6 (.in_1(n8buffer_8_out_2), .out_2(ReadRamFlag));

  assign out_6 = {Data_from_Reg1, Data_from_Reg2};
  assign SaveRamData = DataFromCache;

  // Notes on the sheet:
  //   REG1+REG2
  //   LDI
  //   LDIC
  //   MCR
  //   MCM
  //   MMC
  //   CLC
  //   CLR
  //   CLM
  //   CLF
  //   REBOOT
  //   MCMR
  //   MMCR
endmodule

module RAM_Controller (
  input  [7:0] ReadFromRam,
  input  [7:0] SaveToData,
  input  [15:0] AddressToRAM,
  input  LoadRAM,
  input  SaveRAM,
  output [7:0] ToMM,
  output [7:0] SaveToRAM_prime_sData,
  output [15:0] AddressToRAM_2,
  output str,
  output clk,
  output ldr
);

  wire buffer_1_out, n2buffer_1_out_2, n2buffer_2_out_2, n2buffer_3_out_2;

  Register register_1 (.D(ReadFromRam), .en(1'b1), .Q(ToMM), .clk(n2buffer_1_out_2));  // open: clr
  _2Buffer u_2buffer_1 (.in_1(n2buffer_2_out_2), .out_2(n2buffer_1_out_2));
  _2Buffer u_2buffer_2 (.in_1(n2buffer_3_out_2), .out_2(n2buffer_2_out_2));
  _2Buffer u_2buffer_3 (.in_1(LoadRAM), .out_2(n2buffer_3_out_2));
  CLICK click_1 (.in_1(buffer_1_out), .out_2(clk));
  buf buffer_1 (buffer_1_out, SaveRAM);

  assign AddressToRAM_2 = AddressToRAM;
  assign ldr = LoadRAM;
  assign SaveToRAM_prime_sData = SaveToData;
  assign str = SaveRAM;
endmodule

module Comparer (
  input  CLF,
  input  [7:0] FromA,
  input  [7:0] FromB,
  input  CMP,
  output BT,
  output EQ,
  output ST
);

  wire click_1_out_2, click_2_out_2, n2buffer_1_out_2, n2buffer_2_out_2, n2buffer_3_out_2, n2buffer_4_out_2,
       n2buffer_5_out_2, n8buffer_1_out_2, or_1_out;
  wire [2:0] comparator_1_gt;
  wire [7:0] chooser_8bit_1_out_3, chooser_8bit_2_out_3;

  _2Buffer u_2buffer_1 (.in_1(n2buffer_2_out_2), .out_2(n2buffer_1_out_2));
  _2Buffer u_2buffer_2 (.in_1(CMP), .out_2(n2buffer_2_out_2));
  _8Buffer u_8buffer_1 (.in_1(n2buffer_1_out_2), .out_2(n8buffer_1_out_2));
  Chooser_8Bit chooser_8bit_1 (.in_1(n8buffer_1_out_2), .in_2(FromA), .out_3(chooser_8bit_1_out_3));
  Chooser_8Bit chooser_8bit_2 (.in_1(n8buffer_1_out_2), .in_2(FromB), .out_3(chooser_8bit_2_out_3));
  Comparator #(.mode("unsigned")) comparator_1 (
    .a(chooser_8bit_1_out_3), .b(chooser_8bit_2_out_3), .gt(comparator_1_gt[0]), .eq(comparator_1_gt[1]),
    .lt(comparator_1_gt[2]));
  _2Buffer u_2buffer_3 (.in_1(n8buffer_1_out_2), .out_2(n2buffer_3_out_2));
  _2Buffer u_2buffer_4 (.in_1(n2buffer_3_out_2), .out_2(n2buffer_4_out_2));
  CLICK click_1 (.in_1(n8buffer_1_out_2), .out_2(click_1_out_2));
  CLICK click_2 (.in_1(n2buffer_5_out_2), .out_2(click_2_out_2));
  _2Buffer u_2buffer_5 (.in_1(n2buffer_4_out_2), .out_2(n2buffer_5_out_2));
  or or_1 (or_1_out, click_1_out_2, CLF);
  Register #(.width(3)) register_1 (
    .D(comparator_1_gt), .en(n8buffer_1_out_2), .Q({ST, EQ, BT}), .clk(click_2_out_2), .clr(or_1_out));
endmodule

module RS (
  input  R,
  input  S,
  output Q
);

  wire not_2_out, or_1_out, or_2_out;

  or or_1 (or_1_out, R, not_2_out);
  not not_1 (Q, or_1_out);
  or or_2 (or_2_out, Q, S);
  not not_2 (not_2_out, or_2_out);
endmodule

module Jump_Controller (
  input  BT,
  input  EQ,
  input  ST,
  input  [7:0] FromReg1,
  input  [7:0] FromReg2,
  input  [23:0] Command,
  output ReadRegFlag,
  output JmpFlag,
  output JmpClk,
  output [15:0] AddressToJump,
  output [3:0] Reg1Address,
  output [3:0] Reg2Address
);

  wire and_1_out, and_2_out, and_3_out, and_4_out, and_5_out, and_6_out, and_7_out, and_8_out,
       comparator_1_eq, comparator_2_eq, comparator_3_eq, comparator_4_eq, comparator_5_eq, comparator_6_eq,
       comparator_7_eq, comparator_8_eq, comparator_9_eq, comparator_10_eq, n2buffer_1_out_2,
       n2buffer_2_out_2, n2buffer_3_out_2, n2buffer_4_out_2, n2buffer_6_out_2, n8buffer_1_out_2,
       n8buffer_2_out_2, n8buffer_3_out_2, or_1_out, or_2_out, or_3_out, or_4_out, or_5_out;
  wire [3:0] bit_extender_1_out, bit_extender_2_out;
  wire [15:0] and_11_out, and_12_out, bit_extender_3_out, bit_extender_4_out;

  Comparator comparator_1 (.a(Command[23:16]), .b(8'h31), .eq(comparator_1_eq));  // open: gt, lt
  Comparator comparator_2 (.a(Command[23:16]), .b(8'h32), .eq(comparator_2_eq));  // open: gt, lt
  Comparator comparator_3 (.a(Command[23:16]), .b(8'h33), .eq(comparator_3_eq));  // open: gt, lt
  Comparator comparator_4 (.a(Command[23:16]), .b(8'h34), .eq(comparator_4_eq));  // open: gt, lt
  Comparator comparator_5 (.a(Command[23:16]), .b(8'h35), .eq(comparator_5_eq));  // open: gt, lt
  Comparator comparator_6 (.a(Command[23:16]), .b(8'h36), .eq(comparator_6_eq));  // open: gt, lt
  Comparator comparator_7 (.a(Command[23:16]), .b(8'h37), .eq(comparator_7_eq));  // open: gt, lt
  Comparator comparator_8 (.a(Command[23:16]), .b(8'h38), .eq(comparator_8_eq));  // open: gt, lt
  Comparator comparator_9 (.a(Command[23:16]), .b(8'h39), .eq(comparator_9_eq));  // open: gt, lt
  Comparator comparator_10 (.a(Command[23:16]), .b(8'h3a), .eq(comparator_10_eq));  // open: gt, lt
  assign bit_extender_1_out = {{3{or_3_out}}, or_3_out};  // Bit_Extender bit_extender_1
  and and_1 (and_1_out, EQ, comparator_3_eq);
  and and_2 (and_2_out, BT, comparator_4_eq);
  and and_3 (and_3_out, ST, comparator_5_eq);
  and and_4 (and_4_out, EQ, comparator_6_eq);
  and and_5 (and_5_out, BT, comparator_7_eq);
  and and_6 (and_6_out, ST, comparator_8_eq);
  or or_1 (or_1_out, BT, ST);
  and and_7 (and_7_out, or_1_out, comparator_9_eq);
  or or_2 (or_2_out, BT, ST);
  and and_8 (and_8_out, or_2_out, comparator_10_eq);
  assign bit_extender_2_out = {{3{or_3_out}}, or_3_out};  // Bit_Extender bit_extender_2
  assign Reg1Address = bit_extender_2_out & Command[11:8];  // AND_Gate and_9, 4 bits wide
  assign Reg2Address = bit_extender_1_out & Command[15:12];  // AND_Gate and_10, 4 bits wide
  or or_3 (or_3_out, comparator_1_eq, and_1_out, and_7_out, and_2_out, and_3_out);
  or or_4 (or_4_out, comparator_2_eq, and_4_out, and_8_out, and_5_out, and_6_out);
  _2Buffer u_2buffer_1 (.in_1(or_3_out), .out_2(n2buffer_1_out_2));
  _2Buffer u_2buffer_2 (.in_1(n2buffer_1_out_2), .out_2(n2buffer_2_out_2));
  _2Buffer u_2buffer_3 (.in_1(or_4_out), .out_2(n2buffer_3_out_2));
  _16TickClick u_16tickclick_1 (.in_1(n2buffer_2_out_2), .out_2(ReadRegFlag));
  _2Buffer u_2buffer_4 (.in_1(n2buffer_3_out_2), .out_2(n2buffer_4_out_2));
  _8Buffer u_8buffer_1 (.in_1(n8buffer_3_out_2), .out_2(n8buffer_1_out_2));
  _8Buffer u_8buffer_2 (.in_1(n8buffer_1_out_2), .out_2(n8buffer_2_out_2));
  _8Buffer u_8buffer_3 (.in_1(n2buffer_2_out_2), .out_2(n8buffer_3_out_2));
  or or_5 (or_5_out, n2buffer_4_out_2, n8buffer_2_out_2);
  _2Buffer u_2buffer_5 (.in_1(or_5_out), .out_2(JmpFlag));
  assign bit_extender_3_out = {{15{n8buffer_2_out_2}}, n8buffer_2_out_2};  // Bit_Extender bit_extender_3
  assign and_11_out = bit_extender_3_out & {FromReg1, FromReg2};  // AND_Gate and_11, 16 bits wide
  assign bit_extender_4_out = {{15{or_4_out}}, or_4_out};  // Bit_Extender bit_extender_4
  _2Buffer u_2buffer_6 (.in_1(JmpFlag), .out_2(n2buffer_6_out_2));
  assign AddressToJump = and_12_out | and_11_out;  // OR_Gate or_6, 16 bits wide
  assign and_12_out = bit_extender_4_out & Command[15:0];  // AND_Gate and_12, 16 bits wide
  CLICK click_1 (.in_1(n2buffer_6_out_2), .out_2(JmpClk));

  // Notes on the sheet:
  //   JMP
  //   JMPI
  //   JEQ
  //   JBT
  //   JST
  //   JEQI
  //   JBTI
  //   JSTI
  //   JNEQ
  //   JNEQI
endmodule

module Bit_Controller (
  input  TempFlag,
  input  [7:0] Volum0,
  input  [7:0] Volum1,
  output [7:0] Result
);

  wire and_1_out, and_2_out, and_3_out, and_4_out, and_5_out, and_6_out, and_7_out, and_8_out, and_9_out,
       and_10_out, and_11_out, and_12_out, and_13_out, and_14_out, and_15_out, and_16_out, xor_1_out,
       xor_2_out, xor_3_out, xor_4_out, xor_5_out, xor_6_out, xor_7_out, xor_8_out;

  and and_1 (and_1_out, Volum0[0], xor_1_out);
  xor xor_1 (xor_1_out, 1'b1, Volum1[0]);
  and and_2 (and_2_out, Volum0[1], xor_2_out);
  xor xor_2 (xor_2_out, 1'b1, Volum1[1]);
  and and_3 (and_3_out, Volum0[2], xor_3_out);
  xor xor_3 (xor_3_out, 1'b1, Volum1[2]);
  and and_4 (and_4_out, Volum0[3], xor_4_out);
  xor xor_4 (xor_4_out, 1'b1, Volum1[3]);
  and and_5 (and_5_out, Volum0[4], xor_5_out);
  xor xor_5 (xor_5_out, 1'b1, Volum1[4]);
  and and_6 (and_6_out, Volum0[5], xor_6_out);
  xor xor_6 (xor_6_out, 1'b1, Volum1[5]);
  and and_7 (and_7_out, Volum0[6], xor_7_out);
  xor xor_7 (xor_7_out, 1'b1, Volum1[6]);
  and and_8 (and_8_out, Volum0[7], xor_8_out);
  xor xor_8 (xor_8_out, 1'b1, Volum1[7]);
  or or_1 (Result[0], and_1_out, and_9_out);
  and and_9 (and_9_out, Volum1[0], TempFlag);
  or or_2 (Result[1], and_2_out, and_10_out);
  and and_10 (and_10_out, Volum1[1], TempFlag);
  or or_3 (Result[2], and_3_out, and_11_out);
  and and_11 (and_11_out, Volum1[2], TempFlag);
  or or_4 (Result[3], and_4_out, and_12_out);
  and and_12 (and_12_out, Volum1[3], TempFlag);
  or or_5 (Result[4], and_5_out, and_13_out);
  and and_13 (and_13_out, Volum1[4], TempFlag);
  or or_6 (Result[5], and_6_out, and_14_out);
  and and_14 (and_14_out, Volum1[5], TempFlag);
  or or_7 (Result[6], and_7_out, and_15_out);
  and and_15 (and_15_out, Volum1[6], TempFlag);
  or or_8 (Result[7], and_8_out, and_16_out);
  and and_16 (and_16_out, Volum1[7], TempFlag);
endmodule

module Flag_Cogtroller (
  input  SetFlag,
  input  ClearFlag,
  input  BT,
  input  EQ,
  input  ST,
  input  [23:0] Command,
  output TempFlag
);

  wire and_1_out, and_2_out, and_3_out, comparator_1_eq, comparator_2_eq, comparator_3_eq, comparator_4_eq,
       comparator_5_eq, n2buffer_1_out_2, n2buffer_2_out_2, n2buffer_3_out_2, n2buffer_4_out_2,
       n2buffer_5_out_2, n2buffer_6_out_2, n16tickclick_1_out_2, n16tickclick_2_out_2, n16tickclick_3_out_2,
       n16tickclick_4_out_2, n16tickclick_5_out_2, n16tickclick_6_out_2, n16tickclick_7_out_2,
       n16tickclick_8_out_2, n16tickclick_9_out_2, or_1_out, or_2_out;

  Comparator comparator_1 (.a(Command[23:16]), .b(8'h41), .eq(comparator_1_eq));  // open: gt, lt
  Comparator comparator_2 (.a(Command[23:16]), .b(8'h42), .eq(comparator_2_eq));  // open: gt, lt
  Comparator comparator_3 (.a(Command[23:16]), .b(8'h43), .eq(comparator_3_eq));  // open: gt, lt
  Comparator comparator_4 (.a(Command[23:16]), .b(8'h44), .eq(comparator_4_eq));  // open: gt, lt
  Comparator comparator_5 (.a(Command[23:16]), .b(8'h45), .eq(comparator_5_eq));  // open: gt, lt
  and and_1 (and_1_out, EQ, comparator_3_eq);
  and and_2 (and_2_out, BT, comparator_4_eq);
  and and_3 (and_3_out, ST, comparator_5_eq);
  _16TickClick u_16tickclick_1 (.in_1(comparator_1_eq), .out_2(n16tickclick_1_out_2));
  _16TickClick u_16tickclick_2 (.in_1(n2buffer_2_out_2), .out_2(n16tickclick_2_out_2));
  _2Buffer u_2buffer_1 (.in_1(and_1_out), .out_2(n2buffer_1_out_2));
  _2Buffer u_2buffer_2 (.in_1(n2buffer_1_out_2), .out_2(n2buffer_2_out_2));
  _2Buffer u_2buffer_3 (.in_1(n2buffer_4_out_2), .out_2(n2buffer_3_out_2));
  _2Buffer u_2buffer_4 (.in_1(and_2_out), .out_2(n2buffer_4_out_2));
  _16TickClick u_16tickclick_3 (.in_1(n2buffer_3_out_2), .out_2(n16tickclick_3_out_2));
  _16TickClick u_16tickclick_4 (.in_1(n2buffer_6_out_2), .out_2(n16tickclick_4_out_2));
  _2Buffer u_2buffer_5 (.in_1(and_3_out), .out_2(n2buffer_5_out_2));
  _2Buffer u_2buffer_6 (.in_1(n2buffer_5_out_2), .out_2(n2buffer_6_out_2));
  _16TickClick u_16tickclick_5 (.in_1(comparator_2_eq), .out_2(n16tickclick_5_out_2));
  _16TickClick u_16tickclick_6 (.in_1(comparator_3_eq), .out_2(n16tickclick_6_out_2));
  _16TickClick u_16tickclick_7 (.in_1(ClearFlag), .out_2(n16tickclick_7_out_2));
  _16TickClick u_16tickclick_8 (.in_1(comparator_4_eq), .out_2(n16tickclick_8_out_2));
  _16TickClick u_16tickclick_9 (.in_1(comparator_5_eq), .out_2(n16tickclick_9_out_2));
  or or_1 (or_1_out, n16tickclick_1_out_2, n16tickclick_2_out_2, SetFlag, n16tickclick_3_out_2, n16tickclick_4_out_2);
  or or_2 (or_2_out, n16tickclick_5_out_2, n16tickclick_6_out_2, n16tickclick_7_out_2, n16tickclick_8_out_2, n16tickclick_9_out_2);
  RS rs_1 (.R(or_2_out), .S(or_1_out), .Q(TempFlag));

  // Notes on the sheet:
  //   STH
  //   STL
  //   SEQ
  //   SBT
  //   SST
endmodule

module GPIO (
  input  [7:0] DataFromRAMC,
  input  str,
  input  [15:0] AddressFromRAMC,
  input  [15:0] SetAddress,
  input  clk,
  output _0,
  output _1,
  output _2,
  output _3,
  output _4,
  output _5,
  output _6,
  output _7
);

  wire and_1_out, comparator_1_eq, n2buffer_1_out_2, n2buffer_2_out_2;

  and and_1 (and_1_out, str, comparator_1_eq);
  Comparator #(.width(16), .mode("unsigned")) comparator_1 (
    .a(AddressFromRAMC), .b(SetAddress), .eq(comparator_1_eq));  // open: gt, lt
  Register register_1 (
    .D(DataFromRAMC), .en(and_1_out), .Q({_7, _6, _5, _4, _3, _2, _1, _0}), .clk(n2buffer_1_out_2));  // open: clr
  _2Buffer u_2buffer_1 (.in_1(n2buffer_2_out_2), .out_2(n2buffer_1_out_2));
  _2Buffer u_2buffer_2 (.in_1(clk), .out_2(n2buffer_2_out_2));
endmodule

module Display (
  input  [15:0] Address,
  input  [7:0] Data,
  input  STR,
  input  CLK,
  input  [15:0] StartAddress,
  output [7:0] _0,
  output [7:0] _1,
  output [7:0] _2,
  output [7:0] _3,
  output [7:0] _4,
  output [7:0] _5,
  output [7:0] _6,
  output [7:0] _7
);

  wire [15:0] adder_1_out, adder_2_out, adder_3_out, adder_4_out, adder_5_out, adder_6_out, adder_7_out;

  GPIO gpio_1 (
    .DataFromRAMC(Data), .str(STR), .AddressFromRAMC(Address), .SetAddress(StartAddress), .clk(CLK),
    ._0(_0[0]), ._1(_0[1]), ._2(_0[2]), ._3(_0[3]), ._4(_0[4]), ._5(_0[5]), ._6(_0[6]), ._7(_0[7]));
  Adder #(.width(16)) adder_1 (.a(StartAddress), .b(16'h1), .out(adder_1_out));  // open: cin, cout
  GPIO gpio_2 (
    .DataFromRAMC(Data), .str(STR), .AddressFromRAMC(Address), .SetAddress(adder_1_out), .clk(CLK),
    ._0(_1[0]), ._1(_1[1]), ._2(_1[2]), ._3(_1[3]), ._4(_1[4]), ._5(_1[5]), ._6(_1[6]), ._7(_1[7]));
  Adder #(.width(16)) adder_2 (.a(adder_1_out), .b(16'h1), .out(adder_2_out));  // open: cin, cout
  GPIO gpio_3 (
    .DataFromRAMC(Data), .str(STR), .AddressFromRAMC(Address), .SetAddress(adder_2_out), .clk(CLK),
    ._0(_2[0]), ._1(_2[1]), ._2(_2[2]), ._3(_2[3]), ._4(_2[4]), ._5(_2[5]), ._6(_2[6]), ._7(_2[7]));
  Adder #(.width(16)) adder_3 (.a(adder_2_out), .b(16'h1), .out(adder_3_out));  // open: cin, cout
  GPIO gpio_4 (
    .DataFromRAMC(Data), .str(STR), .AddressFromRAMC(Address), .SetAddress(adder_3_out), .clk(CLK),
    ._0(_3[0]), ._1(_3[1]), ._2(_3[2]), ._3(_3[3]), ._4(_3[4]), ._5(_3[5]), ._6(_3[6]), ._7(_3[7]));
  Adder #(.width(16)) adder_4 (.a(adder_3_out), .b(16'h1), .out(adder_4_out));  // open: cin, cout
  GPIO gpio_5 (
    .DataFromRAMC(Data), .str(STR), .AddressFromRAMC(Address), .SetAddress(adder_4_out), .clk(CLK),
    ._0(_4[0]), ._1(_4[1]), ._2(_4[2]), ._3(_4[3]), ._4(_4[4]), ._5(_4[5]), ._6(_4[6]), ._7(_4[7]));
  Adder #(.width(16)) adder_5 (.a(adder_4_out), .b(16'h1), .out(adder_5_out));  // open: cin, cout
  GPIO gpio_6 (
    .DataFromRAMC(Data), .str(STR), .AddressFromRAMC(Address), .SetAddress(adder_5_out), .clk(CLK),
    ._0(_5[0]), ._1(_5[1]), ._2(_5[2]), ._3(_5[3]), ._4(_5[4]), ._5(_5[5]), ._6(_5[6]), ._7(_5[7]));
  Adder #(.width(16)) adder_6 (.a(adder_5_out), .b(16'h1), .out(adder_6_out));  // open: cin, cout
  GPIO gpio_7 (
    .DataFromRAMC(Data), .str(STR), .AddressFromRAMC(Address), .SetAddress(adder_6_out), .clk(CLK),
    ._0(_6[0]), ._1(_6[1]), ._2(_6[2]), ._3(_6[3]), ._4(_6[4]), ._5(_6[5]), ._6(_6[6]), ._7(_6[7]));
  Adder #(.width(16)) adder_7 (.a(adder_6_out), .b(16'h1), .out(adder_7_out));  // open: cin, cout
  GPIO gpio_8 (
    .DataFromRAMC(Data), .str(STR), .AddressFromRAMC(Address), .SetAddress(adder_7_out), .clk(CLK),
    ._0(_7[0]), ._1(_7[1]), ._2(_7[2]), ._3(_7[3]), ._4(_7[4]), ._5(_7[5]), ._6(_7[6]), ._7(_7[7]));

  // Notes on the sheet:
  //   0
  //   1
  //   2
  //   3
  //   4
  //   5
  //   6
  //   7
endmodule

module Bit_To_TempFlag (
  input  [7:0] Volum0,
  input  [7:0] Volum1,
  output Result
);

  wire and_1_out, and_2_out, and_3_out, and_4_out, and_5_out, and_6_out, and_7_out, and_8_out;

  and and_1 (and_1_out, Volum0[0], Volum1[0]);
  and and_2 (and_2_out, Volum0[1], Volum1[1]);
  and and_3 (and_3_out, Volum0[2], Volum1[2]);
  and and_4 (and_4_out, Volum0[3], Volum1[3]);
  or or_1 (Result, and_1_out, and_2_out, and_3_out, and_4_out, and_5_out, and_6_out, and_7_out, and_8_out);
  and and_5 (and_5_out, Volum0[4], Volum1[4]);
  and and_6 (and_6_out, Volum0[5], Volum1[5]);
  and and_7 (and_7_out, Volum0[6], Volum1[6]);
  and and_8 (and_8_out, Volum0[7], Volum1[7]);
endmodule

module Stack (
  input  [7:0] _8BitData,
  input  [15:0] _16BitData,
  input  Push,
  input  Pop,
  output [15:0] Out
);

  wire click_1_out_2, click_2_out_2, n2buffer_1_out_2, n2buffer_2_out_2, n2buffer_3_out_2, n2buffer_4_out_2,
       n2buffer_5_out_2, n8buffer_1_out_2, n8buffer_2_out_2, or_2_out, or_3_out;
  wire [15:0] bit_extender_1_out, counter_1_q, or_1_out, ram_1_data;

  assign bit_extender_1_out = {{8{1'b0}}, _8BitData};  // Bit_Extender bit_extender_1
  _2Buffer u_2buffer_1 (.in_1(Pop), .out_2(n2buffer_1_out_2));
  assign or_1_out = bit_extender_1_out | _16BitData;  // OR_Gate or_1, 16 bits wide
  Counter #(.width(16), .max('hffff), .ongoal("stay")) counter_1 (
    .load(Pop), .count(or_2_out), .Q(counter_1_q), .clk(or_3_out));  // open: D, carry, clr
  or or_2 (or_2_out, Pop, Push);
  or or_3 (or_3_out, n2buffer_4_out_2, n2buffer_2_out_2);
  _2Buffer u_2buffer_2 (.in_1(n2buffer_3_out_2), .out_2(n2buffer_2_out_2));
  _2Buffer u_2buffer_3 (.in_1(Push), .out_2(n2buffer_3_out_2));
  _2Buffer u_2buffer_4 (.in_1(n2buffer_1_out_2), .out_2(n2buffer_4_out_2));
  _8Buffer u_8buffer_1 (.in_1(Pop), .out_2(n8buffer_1_out_2));
  CLICK click_1 (.in_1(n2buffer_5_out_2), .out_2(click_1_out_2));
  _2Buffer u_2buffer_5 (.in_1(Push), .out_2(n2buffer_5_out_2));
  RAM #(.addrWidth(16), .dataWidth(16), .bus("separate")) ram_1 (
    .addr(counter_1_q), .din(or_1_out), .data(ram_1_data), .str(Push), .sel(1'b1), .clk(click_1_out_2),
    .ld(n8buffer_1_out_2));  // open: clr
  CLICK click_2 (.in_1(n8buffer_2_out_2), .out_2(click_2_out_2));
  _8Buffer u_8buffer_2 (.in_1(n8buffer_1_out_2), .out_2(n8buffer_2_out_2));
  Register #(.width(16)) register_1 (.D(ram_1_data), .en(n8buffer_1_out_2), .Q(Out), .clk(click_2_out_2));  // open: clr
endmodule

module Stack_Manager (
);

  Stack stack_1 ();  // open: _8BitData, _16BitData, Push, Pop, Out
endmodule

module Chooser_8Bit (
  input  in_1,
  input  [7:0] in_2,
  output [7:0] out_3
);

  and and_1 (out_3[7], in_2[7], in_1);
  and and_2 (out_3[6], in_2[6], in_1);
  and and_3 (out_3[5], in_2[5], in_1);
  and and_4 (out_3[4], in_2[4], in_1);
  and and_5 (out_3[3], in_2[3], in_1);
  and and_6 (out_3[2], in_2[2], in_1);
  and and_7 (out_3[1], in_2[1], in_1);
  and and_8 (out_3[0], in_2[0], in_1);
endmodule
